// Logisim project ULA.circ as structural Verilog: 3 circuits, main circuit main
module main (
  input  [31:0] Entrada_A,
  input  [31:0] Entrada_B,
  input  [4:0] Seletor,
  output out_4,
  output [31:0] \Saída_S 
);

  wire overflowcontroler_1_overflow, undriven, undriven_2, undriven_3, undriven_4;

  Celula celula_1 (
    .b(Entrada_B[30]), .a(Entrada_A[30]), .Seletor(Seletor), .S(\Saída_S [30]));  // open: Cin, SLL, SRL, Cout
  Celula celula_2 (
    .b(Entrada_B[31]), .a(Entrada_A[31]), .Seletor(Seletor), .S(\Saída_S [31]));  // open: Cin, SLL, SRL, Cout
  Celula celula_3 (
    .b(Entrada_B[28]), .a(Entrada_A[28]), .Seletor(Seletor), .S(\Saída_S [28]));  // open: Cin, SLL, SRL, Cout
  Celula celula_4 (
    .b(Entrada_B[29]), .a(Entrada_A[29]), .Seletor(Seletor), .S(\Saída_S [29]));  // open: Cin, SLL, SRL, Cout
  Celula celula_5 (
    .b(Entrada_B[26]), .a(Entrada_A[26]), .Seletor(Seletor), .S(\Saída_S [26]));  // open: Cin, SLL, SRL, Cout
  Celula celula_6 (
    .b(Entrada_B[27]), .a(Entrada_A[27]), .Seletor(Seletor), .S(\Saída_S [27]));  // open: Cin, SLL, SRL, Cout
  Celula celula_7 (
    .b(Entrada_B[24]), .a(Entrada_A[24]), .Seletor(Seletor), .S(\Saída_S [24]));  // open: Cin, SLL, SRL, Cout
  Celula celula_8 (
    .b(Entrada_B[25]), .a(Entrada_A[25]), .Seletor(Seletor), .S(\Saída_S [25]));  // open: Cin, SLL, SRL, Cout
  Celula celula_9 (
    .b(Entrada_B[23]), .a(Entrada_A[22]), .Seletor(Seletor), .S(\Saída_S [22]));  // open: Cin, SLL, SRL, Cout
  Celula celula_10 (
    .b(Entrada_B[22]), .a(Entrada_A[23]), .Seletor(Seletor), .S(\Saída_S [23]));  // open: Cin, SLL, SRL, Cout
  Celula celula_11 (
    .b(Entrada_B[21]), .a(Entrada_A[20]), .Seletor(Seletor), .S(\Saída_S [20]));  // open: Cin, SLL, SRL, Cout
  Celula celula_12 (
    .b(Entrada_B[20]), .a(Entrada_A[21]), .Seletor(Seletor), .S(\Saída_S [21]));  // open: Cin, SLL, SRL, Cout
  Celula celula_13 (
    .b(Entrada_B[19]), .a(Entrada_A[18]), .Seletor(Seletor), .S(\Saída_S [18]));  // open: Cin, SLL, SRL, Cout
  Celula celula_14 (
    .b(Entrada_B[18]), .a(Entrada_A[19]), .Seletor(Seletor), .S(\Saída_S [19]));  // open: Cin, SLL, SRL, Cout
  Celula celula_15 (
    .b(Entrada_B[17]), .a(Entrada_A[16]), .Seletor(Seletor), .S(\Saída_S [16]));  // open: Cin, SLL, SRL, Cout
  Celula celula_16 (
    .b(Entrada_B[16]), .a(Entrada_A[17]), .Seletor(Seletor), .S(\Saída_S [17]));  // open: Cin, SLL, SRL, Cout
  Celula celula_17 (
    .b(Entrada_B[15]), .a(Entrada_A[14]), .Seletor(Seletor), .S(\Saída_S [14]));  // open: Cin, SLL, SRL, Cout
  Celula celula_18 (
    .b(Entrada_B[14]), .a(Entrada_A[15]), .Seletor(Seletor), .S(\Saída_S [15]));  // open: Cin, SLL, SRL, Cout
  Celula celula_19 (
    .b(Entrada_B[13]), .a(Entrada_A[12]), .Seletor(Seletor), .S(\Saída_S [12]));  // open: Cin, SLL, SRL, Cout
  Celula celula_20 (
    .b(Entrada_B[12]), .a(Entrada_A[13]), .Seletor(Seletor), .S(\Saída_S [13]));  // open: Cin, SLL, SRL, Cout
  Celula celula_21 (
    .b(Entrada_B[11]), .a(Entrada_A[10]), .Seletor(Seletor), .S(\Saída_S [10]));  // open: Cin, SLL, SRL, Cout
  Celula celula_22 (
    .b(Entrada_B[10]), .a(Entrada_A[11]), .Seletor(Seletor), .S(\Saída_S [11]));  // open: Cin, SLL, SRL, Cout
  Celula celula_23 (
    .b(Entrada_B[9]), .a(Entrada_A[8]), .Seletor(Seletor), .S(\Saída_S [8]));  // open: Cin, SLL, SRL, Cout
  Celula celula_24 (
    .b(Entrada_B[8]), .a(Entrada_A[9]), .Seletor(Seletor), .S(\Saída_S [9]));  // open: Cin, SLL, SRL, Cout
  Celula celula_25 (
    .b(Entrada_B[7]), .a(Entrada_A[6]), .Seletor(Seletor), .S(\Saída_S [6]));  // open: Cin, SLL, SRL, Cout
  Celula celula_26 (
    .Cin(undriven), .b(Entrada_B[6]), .a(Entrada_A[7]), .Seletor(Seletor), .S(\Saída_S [7]));  // open: SLL, SRL, Cout
  Celula celula_27 (
    .b(Entrada_B[5]), .a(Entrada_A[4]), .Seletor(Seletor), .S(\Saída_S [4]));  // open: Cin, SLL, SRL, Cout
  Celula celula_28 (
    .Cin(undriven_2), .b(Entrada_B[4]), .a(Entrada_A[5]), .Seletor(Seletor), .S(\Saída_S [5]), .Cout(undriven));  // open: SLL, SRL
  Celula celula_29 (
    .b(Entrada_B[3]), .a(Entrada_A[2]), .Seletor(Seletor), .S(\Saída_S [2]));  // open: Cin, SLL, SRL, Cout
  Celula celula_30 (
    .Cin(undriven_4), .b(Entrada_B[2]), .a(Entrada_A[3]), .Seletor(Seletor), .S(\Saída_S [3]),
    .Cout(undriven_2));  // open: SLL, SRL
  Celula celula_31 (
    .b(Entrada_B[1]), .a(Entrada_A[0]), .Seletor(Seletor), .S(\Saída_S [0]), .Cout(undriven_3));  // open: Cin, SLL, SRL
  Celula celula_32 (
    .Cin(1'b0), .b(Entrada_B[0]), .a(Entrada_A[1]), .Seletor(Seletor), .S(\Saída_S [1]), .Cout(undriven_4));  // open: SLL, SRL
  OverFlowControler overflowcontroler_1 (
    .Overflow(overflowcontroler_1_overflow), .Cin(undriven_3), .Seletor(Seletor), .a(Entrada_A[0]),
    .b(Entrada_B[1]), .s(\Saída_S [0]));

  // Notes on the sheet:
  //   00000=AND
  //   00001=OR
  //   00010=XOR
  //   00011=NAND
  //   00100=SOMA INT
  //   00101=SOMA NAT
  //   00110=SUBTRAIR
  //   Overflow
endmodule

module Celula (
  input  Cin,
  input  SLL,
  input  SRL,
  input  b,
  input  a,
  input  Cout,
  input  [4:0] Seletor,
  output S
);

  wire adder_1_cout, adder_1_out, and_1_out, and_2_out, nand_1_out, or_1_out, subtractor_1_bout,
       subtractor_1_out, xor_1_out;

  and and_1 (and_1_out, a, b);
  or or_1 (or_1_out, a, b);
  xor xor_1 (xor_1_out, a, b);
  nand nand_1 (nand_1_out, a, b);
  Adder #(.width(1)) adder_1 (.a(a), .b(b), .out(adder_1_out), .cin(Cin), .cout(adder_1_cout));
  Subtractor #(.width(1)) subtractor_1 (.a(a), .b(b), .out(subtractor_1_out), .bin(Cin), .bout(subtractor_1_bout));
  Multiplexer #(.enable("false")) multiplexer_1 (
    .in0(adder_1_cout), .in1(subtractor_1_bout), .out(Cout), .sel(and_2_out));
  and and_2 (and_2_out, ~Seletor[0], Seletor[1], Seletor[2], ~Seletor[3], ~Seletor[4]);  // AND_Gate
  Multiplexer #(.select(5), .enable("false")) multiplexer_2 (
    .in0(and_1_out), .in1(or_1_out), .in2(xor_1_out), .in3(nand_1_out), .in4(adder_1_out), .in5(adder_1_out),
    .in6(subtractor_1_out), .in7(SLL), .in8(SRL), .out(S), .sel(Seletor));  // open: in9, in10, in11, in12, in13, in14, in15, in16, in17, in18, in19, in20, in21, in22, in23, in24, in25, in26, in27, in28, in29, in30, in31

  // Notes on the sheet:
  //   00000=AND
  //   00001=OR
  //   00010=XOR
  //   00011=NAND
  //   00100=SOMA INT
  //   00101=SOMA NAT
  //   00110=SUBTRATOR
  //   00111=DESLOCAMENTO ESQUERDA
  //   01000=DESLOCAMENTO DIREITA
endmodule

module OverFlowControler (
  input  Cin,
  input  a,
  input  b,
  input  s,
  input  [4:0] Seletor,
  output Overflow
);

  wire and_1_out, and_2_out, and_3_out, or_1_out;

  Multiplexer #(.enable("false")) multiplexer_1 (.in0(Cin), .in1(or_1_out), .out(Overflow), .sel(and_1_out));
  and and_1 (and_1_out, Seletor[0], ~Seletor[1], Seletor[2], ~Seletor[3], ~Seletor[4]);  // AND_Gate
  or or_1 (or_1_out, and_2_out, and_3_out);
  and and_2 (and_2_out, a, b, ~s);  // AND_Gate
  and and_3 (and_3_out, ~a, ~b, s);  // AND_Gate

  // Notes on the sheet:
  //   00100 - Soma de Naturais
  //   00101 - Soma de Inteiros
endmodule
